// Logisim project riscvteste.circ as structural Verilog
module comparator_1b (
  input  i_A,
  input  i_B,
  input  i_C_LESS_THAN,
  input  i_C_EQUAL,
  input  i_C_GREATER_THAN,
  output o_GREATER_THAN,
  output o_EQUAL,
  output O_LESS_THAN
);

  wire and_1_out, and_2_out, and_3_out, and_4_out, not_1_out, not_2_out, not_3_out, xor_1_out;

  not not_1 (not_1_out, i_B);
  not not_2 (not_2_out, i_A);
  and and_1 (and_1_out, i_A, not_1_out);
  xor xor_1 (xor_1_out, i_B, i_A);
  and and_2 (and_2_out, not_2_out, i_B);
  and and_3 (and_3_out, and_1_out, i_C_EQUAL);
  not not_3 (not_3_out, xor_1_out);
  and and_4 (and_4_out, and_2_out, i_C_EQUAL);
  or or_1 (o_GREATER_THAN, i_C_GREATER_THAN, and_3_out);
  and and_5 (o_EQUAL, not_3_out, i_C_EQUAL);
  or or_2 (O_LESS_THAN, i_C_LESS_THAN, and_4_out);
endmodule

module comparator_32b (
  input  [31:0] i_A,
  input  [31:0] i_B,
  input  in_3,
  input  in_4,
  input  in_5
);

  wire comparator_1b_1_o_equal, comparator_1b_1_o_greater_than, comparator_1b_1_o_less_than,
       comparator_1b_2_o_equal, comparator_1b_2_o_greater_than, comparator_1b_2_o_less_than,
       comparator_1b_3_o_equal, comparator_1b_3_o_greater_than, comparator_1b_3_o_less_than,
       comparator_1b_4_o_equal, comparator_1b_4_o_greater_than, comparator_1b_4_o_less_than,
       comparator_1b_5_o_equal, comparator_1b_5_o_greater_than, comparator_1b_5_o_less_than,
       comparator_1b_6_o_equal, comparator_1b_6_o_greater_than, comparator_1b_6_o_less_than,
       comparator_1b_7_o_equal, comparator_1b_7_o_greater_than, comparator_1b_7_o_less_than,
       comparator_1b_8_o_equal, comparator_1b_8_o_greater_than, comparator_1b_8_o_less_than,
       comparator_1b_9_o_equal, comparator_1b_9_o_greater_than, comparator_1b_9_o_less_than,
       comparator_1b_10_o_equal, comparator_1b_10_o_greater_than, comparator_1b_10_o_less_than,
       comparator_1b_11_o_equal, comparator_1b_11_o_greater_than, comparator_1b_11_o_less_than,
       comparator_1b_12_o_equal, comparator_1b_12_o_greater_than, comparator_1b_12_o_less_than,
       comparator_1b_13_o_equal, comparator_1b_13_o_greater_than, comparator_1b_13_o_less_than,
       comparator_1b_14_o_equal, comparator_1b_14_o_greater_than, comparator_1b_14_o_less_than,
       comparator_1b_15_o_equal, comparator_1b_15_o_greater_than, comparator_1b_15_o_less_than,
       comparator_1b_16_o_equal, comparator_1b_16_o_greater_than, comparator_1b_16_o_less_than,
       comparator_1b_17_o_equal, comparator_1b_17_o_greater_than, comparator_1b_17_o_less_than,
       comparator_1b_18_o_equal, comparator_1b_18_o_greater_than, comparator_1b_18_o_less_than,
       comparator_1b_19_o_equal, comparator_1b_19_o_greater_than, comparator_1b_19_o_less_than,
       comparator_1b_20_o_equal, comparator_1b_20_o_greater_than, comparator_1b_20_o_less_than,
       comparator_1b_21_o_equal, comparator_1b_21_o_greater_than, comparator_1b_21_o_less_than,
       comparator_1b_22_o_equal, comparator_1b_22_o_greater_than, comparator_1b_22_o_less_than,
       comparator_1b_23_o_equal, comparator_1b_23_o_greater_than, comparator_1b_23_o_less_than, undriven,
       undriven_2, undriven_3, undriven_4, undriven_5, undriven_6, undriven_7, undriven_8, undriven_9,
       undriven_10, undriven_11, undriven_12;

  comparator_1b comparator_1b_1 (
    .i_A(i_A[31]), .i_B(i_B[31]), .i_C_LESS_THAN(in_3), .i_C_EQUAL(in_4), .i_C_GREATER_THAN(in_5),
    .o_GREATER_THAN(comparator_1b_1_o_greater_than), .o_EQUAL(comparator_1b_1_o_equal),
    .O_LESS_THAN(comparator_1b_1_o_less_than));
  comparator_1b comparator_1b_2 (
    .i_A(i_A[23]), .i_B(i_B[23]), .i_C_LESS_THAN(comparator_1b_22_o_less_than),
    .i_C_EQUAL(comparator_1b_22_o_equal), .i_C_GREATER_THAN(comparator_1b_22_o_greater_than),
    .o_GREATER_THAN(comparator_1b_2_o_greater_than), .o_EQUAL(comparator_1b_2_o_equal),
    .O_LESS_THAN(comparator_1b_2_o_less_than));
  comparator_1b comparator_1b_3 (
    .i_A(undriven_5), .i_B(i_B[15]), .i_C_LESS_THAN(comparator_1b_23_o_less_than),
    .i_C_EQUAL(comparator_1b_23_o_equal), .i_C_GREATER_THAN(comparator_1b_23_o_greater_than),
    .o_GREATER_THAN(comparator_1b_3_o_greater_than), .o_EQUAL(comparator_1b_3_o_equal),
    .O_LESS_THAN(comparator_1b_3_o_less_than));
  comparator_1b comparator_1b_4 (
    .i_A(i_A[30]), .i_B(i_B[30]), .i_C_LESS_THAN(comparator_1b_1_o_less_than),
    .i_C_EQUAL(comparator_1b_1_o_equal), .i_C_GREATER_THAN(comparator_1b_1_o_greater_than),
    .o_GREATER_THAN(comparator_1b_4_o_greater_than), .o_EQUAL(comparator_1b_4_o_equal),
    .O_LESS_THAN(comparator_1b_4_o_less_than));
  comparator_1b comparator_1b_5 (
    .i_A(i_A[22]), .i_B(i_B[22]), .i_C_LESS_THAN(comparator_1b_2_o_less_than),
    .i_C_EQUAL(comparator_1b_2_o_equal), .i_C_GREATER_THAN(comparator_1b_2_o_greater_than),
    .o_GREATER_THAN(comparator_1b_5_o_greater_than), .o_EQUAL(comparator_1b_5_o_equal),
    .O_LESS_THAN(comparator_1b_5_o_less_than));
  comparator_1b comparator_1b_6 (
    .i_A(undriven_6), .i_B(i_B[14]), .i_C_LESS_THAN(comparator_1b_3_o_less_than),
    .i_C_EQUAL(comparator_1b_3_o_equal), .i_C_GREATER_THAN(comparator_1b_3_o_greater_than),
    .o_GREATER_THAN(comparator_1b_6_o_greater_than), .o_EQUAL(comparator_1b_6_o_equal),
    .O_LESS_THAN(comparator_1b_6_o_less_than));
  comparator_1b comparator_1b_7 (
    .i_A(i_A[29]), .i_B(i_B[29]), .i_C_LESS_THAN(comparator_1b_4_o_less_than),
    .i_C_EQUAL(comparator_1b_4_o_equal), .i_C_GREATER_THAN(comparator_1b_4_o_greater_than),
    .o_GREATER_THAN(comparator_1b_7_o_greater_than), .o_EQUAL(comparator_1b_7_o_equal),
    .O_LESS_THAN(comparator_1b_7_o_less_than));
  comparator_1b comparator_1b_8 (
    .i_A(i_A[21]), .i_B(i_B[21]), .i_C_LESS_THAN(comparator_1b_5_o_less_than),
    .i_C_EQUAL(comparator_1b_5_o_equal), .i_C_GREATER_THAN(comparator_1b_5_o_greater_than),
    .o_GREATER_THAN(comparator_1b_8_o_greater_than), .o_EQUAL(comparator_1b_8_o_equal),
    .O_LESS_THAN(comparator_1b_8_o_less_than));
  comparator_1b comparator_1b_9 (
    .i_A(undriven_7), .i_B(undriven), .i_C_LESS_THAN(comparator_1b_6_o_less_than),
    .i_C_EQUAL(comparator_1b_6_o_equal), .i_C_GREATER_THAN(comparator_1b_6_o_greater_than),
    .o_GREATER_THAN(comparator_1b_9_o_greater_than), .o_EQUAL(comparator_1b_9_o_equal),
    .O_LESS_THAN(comparator_1b_9_o_less_than));
  comparator_1b comparator_1b_10 (
    .i_A(i_A[28]), .i_B(i_B[28]), .i_C_LESS_THAN(comparator_1b_7_o_less_than),
    .i_C_EQUAL(comparator_1b_7_o_equal), .i_C_GREATER_THAN(comparator_1b_7_o_greater_than),
    .o_GREATER_THAN(comparator_1b_10_o_greater_than), .o_EQUAL(comparator_1b_10_o_equal),
    .O_LESS_THAN(comparator_1b_10_o_less_than));
  comparator_1b comparator_1b_11 (
    .i_A(i_A[20]), .i_B(i_B[20]), .i_C_LESS_THAN(comparator_1b_8_o_less_than),
    .i_C_EQUAL(comparator_1b_8_o_equal), .i_C_GREATER_THAN(comparator_1b_8_o_greater_than),
    .o_GREATER_THAN(comparator_1b_11_o_greater_than), .o_EQUAL(comparator_1b_11_o_equal),
    .O_LESS_THAN(comparator_1b_11_o_less_than));
  comparator_1b comparator_1b_12 (
    .i_A(undriven_8), .i_B(undriven_2), .i_C_LESS_THAN(comparator_1b_9_o_less_than),
    .i_C_EQUAL(comparator_1b_9_o_equal), .i_C_GREATER_THAN(comparator_1b_9_o_greater_than),
    .o_GREATER_THAN(comparator_1b_12_o_greater_than), .o_EQUAL(comparator_1b_12_o_equal),
    .O_LESS_THAN(comparator_1b_12_o_less_than));
  comparator_1b comparator_1b_13 (
    .i_A(i_A[27]), .i_B(i_B[27]), .i_C_LESS_THAN(comparator_1b_10_o_less_than),
    .i_C_EQUAL(comparator_1b_10_o_equal), .i_C_GREATER_THAN(comparator_1b_10_o_greater_than),
    .o_GREATER_THAN(comparator_1b_13_o_greater_than), .o_EQUAL(comparator_1b_13_o_equal),
    .O_LESS_THAN(comparator_1b_13_o_less_than));
  comparator_1b comparator_1b_14 (
    .i_A(i_A[19]), .i_B(i_B[19]), .i_C_LESS_THAN(comparator_1b_11_o_less_than),
    .i_C_EQUAL(comparator_1b_11_o_equal), .i_C_GREATER_THAN(comparator_1b_11_o_greater_than),
    .o_GREATER_THAN(comparator_1b_14_o_greater_than), .o_EQUAL(comparator_1b_14_o_equal),
    .O_LESS_THAN(comparator_1b_14_o_less_than));
  comparator_1b comparator_1b_15 (
    .i_A(undriven_9), .i_B(undriven_3), .i_C_LESS_THAN(comparator_1b_12_o_less_than),
    .i_C_EQUAL(comparator_1b_12_o_equal), .i_C_GREATER_THAN(comparator_1b_12_o_greater_than),
    .o_GREATER_THAN(comparator_1b_15_o_greater_than), .o_EQUAL(comparator_1b_15_o_equal),
    .O_LESS_THAN(comparator_1b_15_o_less_than));
  comparator_1b comparator_1b_16 (
    .i_A(i_A[26]), .i_B(i_B[26]), .i_C_LESS_THAN(comparator_1b_13_o_less_than),
    .i_C_EQUAL(comparator_1b_13_o_equal), .i_C_GREATER_THAN(comparator_1b_13_o_greater_than),
    .o_GREATER_THAN(comparator_1b_16_o_greater_than), .o_EQUAL(comparator_1b_16_o_equal),
    .O_LESS_THAN(comparator_1b_16_o_less_than));
  comparator_1b comparator_1b_17 (
    .i_A(i_A[18]), .i_B(i_B[18]), .i_C_LESS_THAN(comparator_1b_14_o_less_than),
    .i_C_EQUAL(comparator_1b_14_o_equal), .i_C_GREATER_THAN(comparator_1b_14_o_greater_than),
    .o_GREATER_THAN(comparator_1b_17_o_greater_than), .o_EQUAL(comparator_1b_17_o_equal),
    .O_LESS_THAN(comparator_1b_17_o_less_than));
  comparator_1b comparator_1b_18 (
    .i_A(undriven_10), .i_B(undriven_4), .i_C_LESS_THAN(comparator_1b_15_o_less_than),
    .i_C_EQUAL(comparator_1b_15_o_equal), .i_C_GREATER_THAN(comparator_1b_15_o_greater_than),
    .o_GREATER_THAN(comparator_1b_18_o_greater_than), .o_EQUAL(comparator_1b_18_o_equal),
    .O_LESS_THAN(comparator_1b_18_o_less_than));
  comparator_1b comparator_1b_19 (
    .i_A(i_A[25]), .i_B(i_B[25]), .i_C_LESS_THAN(comparator_1b_16_o_less_than),
    .i_C_EQUAL(comparator_1b_16_o_equal), .i_C_GREATER_THAN(comparator_1b_16_o_greater_than),
    .o_GREATER_THAN(comparator_1b_19_o_greater_than), .o_EQUAL(comparator_1b_19_o_equal),
    .O_LESS_THAN(comparator_1b_19_o_less_than));
  comparator_1b comparator_1b_20 (
    .i_A(i_A[17]), .i_B(i_B[17]), .i_C_LESS_THAN(comparator_1b_17_o_less_than),
    .i_C_EQUAL(comparator_1b_17_o_equal), .i_C_GREATER_THAN(comparator_1b_17_o_greater_than),
    .o_GREATER_THAN(comparator_1b_20_o_greater_than), .o_EQUAL(comparator_1b_20_o_equal),
    .O_LESS_THAN(comparator_1b_20_o_less_than));
  comparator_1b comparator_1b_21 (
    .i_A(undriven_11), .i_B(i_B[9]), .i_C_LESS_THAN(comparator_1b_18_o_less_than),
    .i_C_EQUAL(comparator_1b_18_o_equal), .i_C_GREATER_THAN(comparator_1b_18_o_greater_than),
    .o_GREATER_THAN(comparator_1b_21_o_greater_than), .o_EQUAL(comparator_1b_21_o_equal),
    .O_LESS_THAN(comparator_1b_21_o_less_than));
  comparator_1b comparator_1b_22 (
    .i_A(i_A[24]), .i_B(i_B[24]), .i_C_LESS_THAN(comparator_1b_19_o_less_than),
    .i_C_EQUAL(comparator_1b_19_o_equal), .i_C_GREATER_THAN(comparator_1b_19_o_greater_than),
    .o_GREATER_THAN(comparator_1b_22_o_greater_than), .o_EQUAL(comparator_1b_22_o_equal),
    .O_LESS_THAN(comparator_1b_22_o_less_than));
  comparator_1b comparator_1b_23 (
    .i_A(i_A[16]), .i_B(i_B[16]), .i_C_LESS_THAN(comparator_1b_20_o_less_than),
    .i_C_EQUAL(comparator_1b_20_o_equal), .i_C_GREATER_THAN(comparator_1b_20_o_greater_than),
    .o_GREATER_THAN(comparator_1b_23_o_greater_than), .o_EQUAL(comparator_1b_23_o_equal),
    .O_LESS_THAN(comparator_1b_23_o_less_than));
  comparator_1b comparator_1b_24 (
    .i_A(undriven_12), .i_B(i_B[8]), .i_C_LESS_THAN(comparator_1b_21_o_less_than),
    .i_C_EQUAL(comparator_1b_21_o_equal), .i_C_GREATER_THAN(comparator_1b_21_o_greater_than));  // open: o_GREATER_THAN, o_EQUAL, O_LESS_THAN
endmodule
